# Fritzing sketch pir_sensor (saved by Fritzing 0.9.3b)
breadboards: 1

parts:
  Composant1 = Arduino Uno (Rev3)
  LED1 = LED - 3mm [color="Red (633nm)" package="3 mm [THT]"]  # not connected
  J1 = Piezo Speaker

nets:
  N1: Composant1.D10_PWM/SS, J1.pin2
  N2: Composant1.GND, J1.pin1
